# Fritzing sketch RPi_HC-SR04_Adapter (saved by Fritzing 0.9.3b)
circuit board: 3.5cm x 1.5cm
breadboards: 1

parts:
  RPi = Generic female header - 4 pins [form="♀ (female)" package=THT]
  HC-SR04 = Generic female header - 4 pins [form="♀ (female)" package=THT]
  R1 = Resistor [tolerance=±5% resistance=470 package=THT]
  330 = Resistor [tolerance=±5% resistance=330 package=THT]

nets:
  GND: RPi.GND, HC-SR04.GND
  VCC: RPi.VCC, HC-SR04.VCC
  N1: RPi.SCL, HC-SR04.SCL, R1.Pin_1, 330.Pin_0, 330.Pin_1
  N2: RPi.SDA, HC-SR04.SDA, R1.Pin_0

notes:
  VCC
  Trig
  Echo
  GND
  HC-SR04 3.3v Converter

custom parts:
  Generic female header - 4 pins: Generic female header
